# Fritzing sketch Schematic (saved by Fritzing 0.9.3b)
breadboards: 1

parts:
  R1 = Resistor [tolerance=±5% resistance=220 package=THT]
  R2 = Resistor [tolerance=±5% resistance=220 package=THT]
  R3 = Resistor [tolerance=±5% resistance=220 package=THT]
  S1 = SWITCH-MOMENTARY-2 [package=reed_switch_plastic]
  S2 = SWITCH-MOMENTARY-2 [package=reed_switch_plastic]
  S3 = SWITCH-MOMENTARY-2 [package=reed_switch_plastic]
  S4 = SWITCH-MOMENTARY-2 [package=reed_switch_plastic]
  S5 = SWITCH-MOMENTARY-2 [package=reed_switch_plastic]
  S6 = SWITCH-MOMENTARY-2 [package=reed_switch_plastic]
  S7 = SWITCH-MOMENTARY-2 [package=reed_switch_plastic]
  S8 = SWITCH-MOMENTARY-2 [package=reed_switch_plastic]
  S9 = SWITCH-MOMENTARY-2 [package=reed_switch_plastic]
  S10 = SWITCH-MOMENTARY-2 [package=reed_switch_plastic]
  S11 = SWITCH-MOMENTARY-2 [package=reed_switch_plastic]
  S12 = SWITCH-MOMENTARY-2 [package=reed_switch_plastic]

nets:
  N1: R1.Pin_0, S1.1, S2.1, S3.1, S6.1
  GND: R1.Pin_1, R2.Pin_1, R3.Pin_1
  N2: R2.Pin_0, S4.1, S5.1, S7.1, S8.1
  N3: R3.Pin_0, S9.1, S10.1, S11.1, S12.1
  N4: S1.2, S4.2, S12.2
  N5: S2.2, S5.2, S9.2
  N6: S3.2, S7.2, S10.2
  N7: S6.2, S8.2, S11.2

notes:
  Filas (0 - 3)
  Rojo
  Columnas (0 - 2)
  Azul
